// Digital circuit Algebra_Overview.dig as structural Verilog
module Algebra_Overview (
  input  e1,
  input  e2,
  input  e3,
  input  e4,
  input  e5,
  output a1,
  output a2,
  output a3
);

  and and_1 (a1, e1, e2);
  or or_1 (a2, e3, e4);
  // Not not_1 has open pins: in=e5, out=open
endmodule
