// Digital circuit Simple_TT_XNOR_FanIn3.dig as structural Verilog
module Simple_TT_XNOR_FanIn3 (
  input  s1,
  input  s2,
  input  s3,
  output l
);

  // XNOr xnor_1 has open pins: In_1=s1, In_2=s2, In_3=s3, out=open
endmodule
