// Digital circuit Simple_TT_XOR_FanIn3_with2.dig as structural Verilog
module Simple_TT_XOR_FanIn3_with2 (
  input  s1,
  input  s2,
  input  s3,
  output l
);

  wire xor_1_out;

  xor xor_1 (xor_1_out, s1, s2);
  xor xor_2 (l, xor_1_out, s3);
endmodule
