// Digital circuit AusdruckSchaltnetz.dig as structural Verilog
module AusdruckSchaltnetz (
  input  x_0,
  input  x_1,
  input  x_2,
  output y
);

  wire and_1_out, and_2_out, and_3_out, not_1_out, or_1_out;

  not not_1 (not_1_out, x_0);
  and and_1 (and_1_out, x_2, not_1_out);
  and and_2 (and_2_out, x_1, not_1_out);
  and and_3 (and_3_out, and_1_out, x_0);
  or or_1 (or_1_out, and_2_out, x_0);
  or or_2 (y, and_3_out, or_1_out);
endmodule

/* Test case:
x_2 x_1 x_0 y
0   0   0   0
0   0   1   1
0   1   0   1
0   1   1   1
1   0   0   0
1   0   1   1
1   1   0   1
1   1   1   1
*/
