// Digital circuit AusdruckSchaltnetz_Step3.dig as structural Verilog
module AusdruckSchaltnetz_Step3 (
  output y
);

  wire and_1_out, or_1_out, undriven, undriven_2, undriven_3, undriven_4;

  and and_1 (and_1_out, undriven, undriven_2);
  or or_1 (or_1_out, undriven_3, undriven_4);
  or or_2 (y, and_1_out, or_1_out);
endmodule
