// Digital circuit AusdruckSchaltnetz_Step4.dig as structural Verilog
module AusdruckSchaltnetz_Step4 (
  input  x_0,
  output y
);

  wire and_1_out, and_2_out, and_3_out, not_1_out, or_1_out, undriven, undriven_2;

  not not_1 (not_1_out, x_0);
  and and_1 (and_1_out, undriven, not_1_out);
  and and_2 (and_2_out, undriven_2, not_1_out);
  and and_3 (and_3_out, and_1_out, x_0);
  or or_1 (or_1_out, and_2_out, x_0);
  or or_2 (y, and_3_out, or_1_out);
endmodule
