// Digital circuit Codierer8zu3.dig as structural Verilog
// 8-zu-3 Codierer (1-aus-8 zu 3-Bit Binär)
module Codierer8zu3 (
  input  e0,
  input  e1,
  input  e2,
  input  e3,
  input  e4,
  input  e5,
  input  e6,
  input  e7,
  output a0,
  output a1,
  output a2
);

  or or_1 (a0, e1, e3, e5, e7);
  or or_2 (a1, e2, e3, e6, e7);
  or or_3 (a2, e4, e5, e6, e7);
endmodule

/* Test case:
e7 e6 e5 e4 e3 e2 e1 e0 a2 a1 a0
0  0  0  0  0  0  0  1  0  0  0
0  0  0  0  0  0  1  0  0  0  1
0  0  0  0  0  1  0  0  0  1  0
0  0  0  0  1  0  0  0  0  1  1
0  0  0  1  0  0  0  0  1  0  0
0  0  1  0  0  0  0  0  1  0  1
0  1  0  0  0  0  0  0  1  1  0
1  0  0  0  0  0  0  0  1  1  1
*/
