// Digital circuit FullAdder.dig as structural Verilog
module FullAdder (
  input  Carry1,
  input  e1,
  input  e2,
  output Carry2,
  output Sum
);

  wire and_1_out, and_2_out, xor_1_out;

  xor xor_1 (xor_1_out, e1, Carry1);
  and and_1 (and_1_out, e1, Carry1);
  xor xor_2 (Sum, xor_1_out, Carry1);
  and and_2 (and_2_out, xor_1_out, Carry1);
  or or_1 (Carry2, and_1_out, and_2_out);

  assign e2 = Carry1;
endmodule
