// Digital circuit FullAdder_Block.dig as structural Verilog
// 1-Bit Volladdierer als modularer Schaltungsblock
module FullAdder_Block (
  input  A_i,
  input  B_i,
  input  C_i_1,
  output C_i,
  output S_i
);

  // FullAdder fulladder_1: pin names not known; wires that end beside it: C_i_1, A_i, S_i, B_i, C_i
endmodule

/* Test case:
A_i B_i C_{i-1} C_i S_i
0   0   0       0   0
0   0   1       0   1
0   1   0       0   1
0   1   1       1   0
1   0   0       0   1
1   0   1       1   0
1   1   0       1   0
1   1   1       1   1
*/
