// Digital circuit HalfAdder.dig as structural Verilog
module HalfAdder (
  input  e1,
  input  e2,
  output Carry,
  output Sum
);

  xor xor_1 (Sum, e1, e1);
  and and_1 (Carry, e1, e1);

  assign e2 = e1;
endmodule
