// Digital circuit VierBitAddierer.dig as structural Verilog
// Simplified 4-bit ripple carry adder, consisting of four full adders.
// {{de Vereinfachter 4-Bit Ripple-Carry-Addierer, bestehend
// aus vier Volladdierern.}}
module VierBitAddierer (
  input  A_0,
  input  B_0,
  input  A_1,
  input  B_1,
  input  A_2,
  input  B_2,
  input  A_3,
  input  B_3,
  input  C__1,
  output S_0,
  output S_1,
  output S_2,
  output S_3,
  output C_3
);

  wire volladdierer_1_p5, volladdierer_2_p5, volladdierer_3_p5;

  // Volladdierer volladdierer_1: pin names not known; wires that end beside it: C__1, A_0, S_0, B_0, volladdierer_1_p5
  // Volladdierer volladdierer_2: pin names not known; wires that end beside it: volladdierer_1_p5, A_1, S_1, B_1, volladdierer_2_p5
  // Volladdierer volladdierer_3: pin names not known; wires that end beside it: volladdierer_2_p5, A_2, S_2, B_2, volladdierer_3_p5
  // Volladdierer volladdierer_4: pin names not known; wires that end beside it: volladdierer_3_p5, A_3, S_3, B_3, C_3
endmodule

/* Test case:
# complete test of all 512 possible additions
C_{-1} A_3 A_2 A_1 A_0 B_3 B_2 B_1 B_0 C_3 S_3 S_2 S_1 S_0
loop(A,16)
  loop(B,16)
0 bits(4,A) bits(4,B) bits(5,A+B)
1 bits(4,A) bits(4,B) bits(5,A+B+1)
  end loop
end loop
*/
