// Digital circuit Volladdierer.dig as structural Verilog
module Volladdierer (
  input  e1,
  input  e2,
  input  e3,
  output a1,
  output a2
);

  wire and_1_out, and_2_out, xor_1_out;

  xor xor_1 (xor_1_out, e1, e2);
  and and_1 (and_1_out, e1, e2);
  xor xor_2 (a1, xor_1_out, e2);
  and and_2 (and_2_out, xor_1_out, e2);
  or or_1 (a2, and_1_out, and_2_out);

  assign e3 = e2;
endmodule
