// Digital circuit priorityencoder.dig as structural Verilog
module priorityencoder (
  input  e0,
  input  e1,
  input  e2,
  input  e3,
  output a0,
  output a1,
  output v
);

  wire and_1_out, and_2_out;

  not not_1 (e1, e2);
  not not_2 (e1, e1);
  // Or or_1 has open pins: In_1=e0, In_2=e1, In_3=e1, In_4=open, out=open
  and and_1 (and_1_out, e2, e1);
  and and_2 (and_2_out, e1, e1, e1);
  or or_2 (a0, and_1_out, e1);
  or or_3 (a1, and_2_out, e1);

  assign e3 = e1;
endmodule
