// Digital circuit ti2_mux.dig as structural Verilog
module ti2_mux (
  input  Constant,
  input  Constant1,
  input  S0,
  input  S1,
  input  e0,
  input  e1,
  input  e2,
  input  e3,
  output a
);

  wire and_1_out, and_2_out, and_3_out, and_4_out, not_2_out;

  not not_1 (S0, S0);
  not not_2 (not_2_out, S0);
  and and_1 (and_1_out, not_2_out, e0, S0);
  and and_2 (and_2_out, S0, e1, S0);
  and and_3 (and_3_out, not_2_out, e2, S0);
  and and_4 (and_4_out, S0, e3, S0);
  // Or or_1 has open pins: In_1=and_1_out, In_2=and_2_out, In_3=and_4_out, In_4=open, out=open

  assign S1 = S0;
endmodule
