// Digital circuit LogikHazard.dig as structural Verilog
module LogikHazard (
  input  x1,
  input  x2,
  input  x3,
  input  x4,
  output Display5,
  output Display6,
  output Display7,
  output Display8
);

  wire and_2_out, not_3_out, not_4_out;

  // Not not_1 has open pins: in=x1, out=open
  // Not not_2 has open pins: in=x2, out=open
  not not_3 (not_3_out, x3);
  not not_4 (not_4_out, x4);
  // And and_1 has open pins: In_1=x3, In_2=not_4_out, out=open
  // Or or_1 has open pins: In_1=open, In_2=and_2_out, out=open
  and and_2 (and_2_out, x1, x2, not_3_out);

  assign Display5 = x1;
  assign Display6 = x2;
  assign Display7 = x3;
  assign Display8 = x4;
endmodule
