// Digital circuit dynhazard.dig as structural Verilog
module dynhazard (
  input  x1,
  input  x2,
  input  x3,
  output y
);

  wire and_1_out, and_2_out, delay_1_out, delay_2_out, not_1_out, or_1_out;

  or or_1 (or_1_out, x1, x2);
  and and_1 (and_1_out, x2, x3);
  Delay #(.delayTime(1)) delay_1 (.in(and_1_out), .out(delay_1_out));
  Delay #(.delayTime(7)) delay_2 (.in(or_1_out), .out(delay_2_out));
  not not_1 (not_1_out, delay_1_out);
  and and_2 (and_2_out, x2, not_1_out);
  or or_2 (y, delay_2_out, and_2_out);

  // Notes on the sheet:
  //   x3: default 1
endmodule
