// Digital circuit funktionshazard_loesung.dig as structural Verilog
module funktionshazard_loesung (
  input  x1,
  input  x2,
  input  x3,
  input  x4,
  output y
);

  wire and_1_out, and_2_out, undriven;

  Delay #(.delayTime(20)) delay_1 ();  // open: in, out
  Delay #(.delayTime(20)) delay_2 ();  // open: in, out
  buf and_1 (and_1_out, x3);  // And open: In_2
  and and_2 (and_2_out, undriven, x2, x3);
  or or_1 (y, and_1_out, and_2_out);
endmodule
