// Digital circuit hazard.dig as structural Verilog
module hazard (
  input  Constant,
  input  Constant1,
  input  Manual_Switch1,
  input  Manual_Switch2,
  input  Manual_Switch3,
  input  x4
);

  wire and_1_out, and_2_out, and_3_out, and_4_out, not_1_out, not_2_out;

  not not_1 (not_1_out, Manual_Switch2);
  not not_2 (not_2_out, Manual_Switch1);
  and and_1 (and_1_out, Manual_Switch3, not_1_out, Manual_Switch1);
  and and_2 (and_2_out, Manual_Switch3, not_2_out, Manual_Switch2);
  and and_3 (and_3_out, Manual_Switch1, Manual_Switch1);
  and and_4 (and_4_out, Manual_Switch2, Manual_Switch1);
  // Or or_1 has open pins: In_1=and_1_out, In_2=and_2_out, In_3=and_4_out, In_4=open, out=open

  assign x4 = Manual_Switch1;
endmodule
