// Digital circuit hazard_tt.dig as structural Verilog
module hazard_tt (
  input  x1,
  input  x2,
  input  x3,
  input  x4,
  output y
);

  wire and_1_out, and_2_out, not_1_out, not_2_out;

  not not_1 (not_1_out, x4);
  not not_2 (not_2_out, x3);
  and and_1 (and_1_out, x3, not_1_out);
  and and_2 (and_2_out, x1, x2, not_2_out);
  or or_1 (y, and_1_out, and_2_out);

  // Notes on the sheet:
  //   x1: default 1
  //   x2: default 1
  //   x3: default 1
endmodule
