// Digital circuit logikhazard_signal.dig as structural Verilog
module logikhazard_signal (
  input  x1,
  input  x2,
  input  x4,
  output Display5,
  output Display6,
  output Display7,
  output Display8,
  output Signal_3
);

  wire not_3_out;

  // Not not_1 has open pins: in=x1, out=open
  // Not not_2 has open pins: in=x2, out=open
  // Not not_3 has open pins: in=open, out=not_3_out
  not not_4 (not_3_out, x4);
  buf and_1 (x2, not_3_out);  // And open: In_1
  // And and_2 has open pins: In_1=x1, In_2=x2, In_3=not_3_out, out=open
  // Or or_1 has open pins: In_1=x2, In_2=open, out=open

  assign Display5 = x1;
  assign Display6 = x2;
  assign Display8 = x4;
endmodule
