// Digital circuit logikhazard_signal_repariert.dig as structural Verilog
module logikhazard_signal_repariert (
  input  x1,
  input  x2,
  input  x4,
  output x3
);

  wire and_2_out, and_3_out, not_1_out, not_2_out;

  // Not not_1 has open pins: in=open, out=not_1_out
  not not_2 (not_2_out, x4);
  // And and_1 has open pins: In_1=x1, In_2=x1, In_3=not_1_out, out=open
  buf and_2 (and_2_out, not_2_out);  // And open: In_1
  and and_3 (and_3_out, x1, x1, not_2_out);
  // Or or_1 has open pins: In_1=and_2_out, In_2=open, In_3=and_3_out, out=open

  assign x2 = x1;
endmodule
