// Digital circuit D_Latch.dig as structural Verilog
// Getaktetes D-Latch
module D_Latch (
  input  D,
  input  C,
  output Q,
  output nQ
);

  wire and_1_out, and_2_out, not_1_out;

  and and_1 (and_1_out, not_1_out, C);
  not not_1 (not_1_out, D);
  and and_2 (and_2_out, C, D);
  nor nor_1 (Q, and_1_out, nQ);
  nor nor_2 (nQ, Q, and_2_out);
endmodule

/* Test case:
C D Q ~Q
C 1 1  0
0 1 1  0
0 0 1  0
C 0 0  1
0 0 0  1
0 1 0  1
*/
