// Digital circuit D_Latch_Block.dig as structural Verilog
// DIN-Blocksymbol des D-Latches
module D_Latch_Block (
  input  D,
  input  C,
  output Q,
  output nQ
);

  D_Latch d_latch_1 (.D(D), .C(C), .Q(Q), .nQ(nQ));
endmodule

/* Test case:
C D Q ~Q
1 0 0  1
0 1 0  1
1 1 1  0
0 0 1  0
1 0 0  1
0 0 0  1
*/
