// Digital circuit MooreAutomat.dig as structural Verilog
module MooreAutomat (
  input  a,
  input  C,
  output o
);

  wire xor_1_out;

  xor xor_1 (xor_1_out, a, o);
  D_FF Zustand__Q (.D(xor_1_out), .C(C), .Q(o));  // open: nQ
endmodule
