// Digital circuit RS_Latch_Block.dig as structural Verilog
// DIN-Blocksymbol des getakteten RS-Latches
module RS_Latch_Block (
  input  S,
  input  C,
  input  R,
  output Q,
  output nQ
);

  RS_Latch_Getaktet rs_latch_getaktet_1 (.S(S), .C(C), .Q(Q), .nQ(nQ), .R(R));
endmodule

/* Test case:
C S R Q ~Q
1 0 1 0  1
0 1 0 0  1
1 1 0 1  0
0 0 1 1  0
1 0 1 0  1
0 0 0 0  1
*/
