// Digital circuit RS_Latch_Getaktet.dig as structural Verilog
// A gated NOR SR latch.
// {{de Einfaches NOR RS-Flipflop mit Freigabeeingang.}}
module RS_Latch_Getaktet (
  input  S,
  input  C,
  input  R,
  output Q,
  output nQ
);

  wire and_1_out, and_2_out;

  and and_1 (and_1_out, R, C);
  and and_2 (and_2_out, C, S);
  nor nor_1 (Q, and_1_out, nQ);
  nor nor_2 (nQ, Q, and_2_out);

  // Notes on the sheet:
  //   S: Set input
  //   {{de Set Eingang}}
  //   C: gate input
  //   {{de Freigabeeingang}}
  //   Q: The stored bit.
  //   {{de Das gespeicherte Bit}}
  //   nQ: The inverted stored bit.
  //   {{de Das inverse des gespeicherten Bits}}
  //   R: Reset input
  //   {{de Reset Eingang}}
endmodule

/* Test case:
R C S Q ~Q
1 C 0 0  1
X 0 X 0  1
0 C 1 1  0
X 0 X 1  0
*/
