// Digital circuit RS_Latch_NAND.dig as structural Verilog
module RS_Latch_NAND (
  input  nS,
  input  nR,
  output Q,
  output nQ
);

  nand nand_1 (Q, nS, nQ);
  nand nand_2 (nQ, Q, nR);
endmodule

/* Test case:
~S ~R Q ~Q
0  1  1  0
1  1  1  0
1  0  0  1
1  1  0  1
*/
