// Digital circuit Register4Bit.dig as structural Verilog
module Register4Bit (
  input  D_0,
  input  D_1,
  input  D_2,
  input  D_3,
  input  C,
  input  EN,
  output Q_0,
  output Q_1,
  output Q_2,
  output Q_3
);

  wire multiplexer_1_out, multiplexer_2_out, multiplexer_3_out, multiplexer_4_out;

  Multiplexer multiplexer_1 (.sel(EN), .in_0(Q_0), .in_1(D_0), .out(multiplexer_1_out));
  Multiplexer multiplexer_2 (.sel(EN), .in_0(Q_1), .in_1(D_1), .out(multiplexer_2_out));
  Multiplexer multiplexer_3 (.sel(EN), .in_0(Q_2), .in_1(D_2), .out(multiplexer_3_out));
  Multiplexer multiplexer_4 (.sel(EN), .in_0(Q_3), .in_1(D_3), .out(multiplexer_4_out));
  D_FF FF_0 (.D(multiplexer_1_out), .C(C), .Q(Q_0));  // open: nQ
  D_FF FF_1 (.D(multiplexer_2_out), .C(C), .Q(Q_1));  // open: nQ
  D_FF FF_2 (.D(multiplexer_3_out), .C(C), .Q(Q_2));  // open: nQ
  D_FF FF_3 (.D(multiplexer_4_out), .C(C), .Q(Q_3));  // open: nQ
endmodule
