// Digital circuit ReversiblerZaehler.dig as structural Verilog
module ReversiblerZaehler (
  input  e,
  input  C,
  output a0,
  output a1
);

  wire and_1_out, and_2_out, and_3_out, and_4_out, not_1_out, not_2_out, not_3_out, or_1_out, or_2_out;

  not not_1 (not_1_out, e);
  not not_2 (not_2_out, a0);
  not not_3 (not_3_out, a1);
  and and_1 (and_1_out, a1, e);
  and and_2 (and_2_out, a0, e);
  and and_3 (and_3_out, not_3_out, not_2_out, e);
  and and_4 (and_4_out, a0, not_1_out);
  or or_1 (or_1_out, and_1_out, and_2_out);
  or or_2 (or_2_out, and_3_out, and_4_out);
  D_FF Z_1_n (.D(or_1_out), .C(C), .Q(a0));  // open: nQ
  D_FF Z_0_n (.D(or_2_out), .C(C), .Q(a1));  // open: nQ
  // Probe z on {e, a0, a1}

  // Other names for the same wires on the sheet: Z_0_n = a1; Z_1_n = a0

  // Notes on the sheet:
  //   C: Hz: 2
endmodule

/* Test case:
C e a0 a1
0 1 0  0
C 1 0  1
C 1 1  0
C 1 1  0
C 0 0  1
C 0 0  0
C 0 0  0
*/
