// Digital circuit Schieberegister4Bit.dig as structural Verilog
// 4-Bit Schieberegister (Serial-In / Parallel-Out)
// {{de 4-Bit Schieberegister mit serieller Eingabe und paralleler Ausgabe}}
module Schieberegister4Bit (
  input  D_in,
  input  C,
  output Q_0,
  output Q_1,
  output Q_2,
  output Q_3,
  output D_out
);

  D_FF FF_0 (.D(D_in), .C(C), .Q(Q_0));  // open: nQ
  D_FF FF_1 (.D(Q_0), .C(C), .Q(Q_1));  // open: nQ
  D_FF FF_2 (.D(Q_1), .C(C), .Q(Q_2));  // open: nQ
  D_FF FF_3 (.D(Q_2), .C(C), .Q(D_out));  // open: nQ

  assign Q_3 = D_out;
endmodule

/* Test case:
C D_in Q_0 Q_1 Q_2 Q_3 D_out
0 1 0 0 0 0 0
C 1 1 0 0 0 0
C 0 0 1 0 0 0
C 1 1 0 1 0 0
C 0 0 1 0 1 1
C 0 0 0 1 0 0
C 0 0 0 0 1 1
C 0 0 0 0 0 0
*/
