// Digital circuit Digital_Counter_Combinatorics.dig as structural Verilog
module Digital_Counter_Combinatorics (
  input  e_0,
  input  e_1,
  input  e_2,
  output a_0,
  output a_1,
  output a_2
);

  wire and_1_out;

  not not_1 (a_0, e_0);
  and and_1 (and_1_out, e_0, e_1);
  xor xor_1 (a_1, e_0, e_1);
  xor xor_2 (a_2, and_1_out, e_2);
endmodule
