// Digital circuit Digital_Counter_Sequential.dig as structural Verilog
module Digital_Counter_Sequential (
  input  C,
  output a_0,
  output a_1,
  output a_2
);

  wire and_1_out, FF_0_q, FF_1_q, FF_2_q;

  D_FF FF_0 (.D(a_0), .C(C), .Q(FF_0_q));  // open: nQ
  D_FF FF_1 (.D(a_1), .C(C), .Q(FF_1_q));  // open: nQ
  D_FF FF_2 (.D(a_2), .C(C), .Q(FF_2_q));  // open: nQ
  not not_1 (a_0, FF_0_q);
  xor xor_1 (a_1, FF_0_q, FF_1_q);
  and and_1 (and_1_out, FF_0_q, FF_1_q);
  xor xor_2 (a_2, and_1_out, FF_2_q);
endmodule
