// Digital circuit Digital_Multiplexer.dig as structural Verilog
// 4-bit multiplexer.
// One of the data bits D_0 to D_3 is output at the output Y. Which 
// output is determined by the two inputs A_0 and A_1.
// {{de Diskret aufgebauter 4-Bit Multiplexer.
// Es wird immer eines der Datenbits D_0 bis D_3 am
// Ausgang Y ausgegeben. Welches ausgegeben wird,
// legen die beiden Eingänge A_0 und A_1 fest.}}
module Digital_Multiplexer (
  input  S_0,
  input  S_1,
  input  e_0,
  input  e_1,
  input  e_2,
  input  e_3,
  output a
);

  wire and_1_out, and_2_out, and_3_out, and_4_out, not_1_out, not_2_out;

  not not_1 (not_1_out, S_1);
  not not_2 (not_2_out, S_0);
  and and_1 (and_1_out, not_2_out, not_1_out, e_0);
  and and_2 (and_2_out, S_0, not_1_out, e_1);
  and and_3 (and_3_out, not_2_out, S_1, e_2);
  and and_4 (and_4_out, S_0, S_1, e_3);
  or or_1 (a, and_1_out, and_2_out, and_3_out, and_4_out);

  // Notes on the sheet:
  //   S_0: Bit 0 of the input selection.
  //   {{de Bit 0 der Signalauswahl.}}
  //   S_1: Bit 1 of the input selection.
  //   {{de Bit 1 der Signalauswahl.}}
  //   e_0: data bit 0.
  //   {{de Das 0. Datenbit.}}
  //   e_1: data bit 1.
  //   {{de Das 1. Datenbit.}}
  //   e_2: data bit 2.
  //   {{de Das 2. Datenbit.}}
  //   e_3: data bit 3.
  //   {{de Das 3. Datenbit.}}
  //   a: Output bit. One of the data bits is always output 
  //   here. Which one is set by the inputs A_0 and A_1.
  //   {{de Ausgangsbit. Es wird immer eines der Datenbits 
  //   hier ausgegeben. Welches das ist, legen die 
  //   Eingänge A_0 und A_1 fest.}}
endmodule
