// Digital circuit Digital_TruthTable_02.dig as structural Verilog
module Digital_TruthTable_02 (
  input  e_1,
  input  e_2,
  input  e_3,
  output a_1,
  output a_2
);

  wire and_1_out, or_1_out, xor_1_out;

  or or_1 (or_1_out, e_1, e_2);
  and and_1 (and_1_out, e_1, e_2);
  and and_2 (a_1, or_1_out, e_3);
  xor xor_1 (xor_1_out, or_1_out, e_3);
  xor xor_2 (a_2, and_1_out, xor_1_out);
endmodule

/* Test case:
e_1 e_2 e_3 a_1 a_2
 0   0   0   0   0
 0   0   1   0   1
 0   1   0   0   1
 0   1   1   1   0
 1   0   0   0   1
 1   0   1   1   0
 1   1   0   0   0
 1   1   1   1   1
*/
